# Fritzing sketch ballroll (saved by Fritzing 0.9.3b)
circuit board: 5.80363cm x 5.8cm
breadboards: 1

parts:
  Part2 = OLED Monochrome 128x64 1.3 inch [part_number=938]
  Part3 = Adafruit ADXL345 [part_number="Adafruit #1231"]
  Part1 = Arduino Micro (Rev3)

nets:
  N1: Part2.MOSI_SDA, Part1.MOSI
  N2: Part2.SCLK_SCK, Part1.SCK
  N3: Part2.DC_SA0, Part1.D6_PWM/A7
  N4: Part2.RESET, Part1.D8_PWM/A8
  N5: Part2.CS, Part1.D7
  VIN: Part2.VIN, Part3.VIN, Part3.CS, Part1.5V
  GND: Part2.GND, Part3.GND, Part3.SDO/ADDR, Part1.GND
  N6: Part3.SDA/SDIO, Part1.D2/SDA
  N7: Part3.SCL, Part1.D3/SCL

custom parts:
  OLED Monochrome 128x64 1.3 inch: These displays are small, only about 1.3" diagonal, but very readable due to the high contrast of an OLED display. This display is made of 128x64 individual white OLED pixels, each one is turned on or off by the controller chip. Because the display makes its own light, no backlight is required. This reduces the power required to run the OLED and is why the display has such high contrast; we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
  Adafruit ADXL345: Filling out our accelerometer offerings, we now have the really lovely digital ADXL345 from Analog Devices, a triple-axis accelerometer with digital I2C and SPI interface breakout. We added an on-board 3.3V regulator and logic-level shifting circuitry, making it a perfect choice for interfacing with any 3V or 5V microcontroller such as the Arduino. The sensor has three axes of measurements, X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
